// Logisim project simple_tmr.circ as structural Verilog: 2 circuits, main circuit main
module main (
  input  in_1,
  input  in_2,
  output out_3,
  output out_4
);

  wire d_ff_1_q, d_ff_2_q, d_ff_3_q, not_1_out, not_2_out, not_3_out;

  D_Flip_Flop d_ff_1 (.D(not_1_out), .clk(in_2), .Q(d_ff_1_q));  // open: Qn, preset, reset
  not not_1 (not_1_out, in_1);
  D_Flip_Flop d_ff_2 (.D(not_2_out), .clk(in_2), .Q(d_ff_2_q));  // open: Qn, preset, reset
  not not_2 (not_2_out, in_1);
  D_Flip_Flop d_ff_3 (.D(not_3_out), .clk(in_2), .Q(d_ff_3_q));  // open: Qn, preset, reset
  not not_3 (not_3_out, in_1);
  majority majority_1 (.a(d_ff_1_q), .b(d_ff_2_q), .c(d_ff_3_q), .outt(out_3), .err(out_4));
endmodule

module majority (
  input  a,
  input  b,
  input  c,
  output outt,
  output err
);

  wire and_1_out, and_2_out, and_3_out, and_4_out, and_5_out, and_6_out, not_1_out, not_2_out, not_3_out;

  not not_1 (not_1_out, a);
  not not_2 (not_2_out, b);
  not not_3 (not_3_out, c);
  and and_1 (and_1_out, b, c);
  and and_2 (and_2_out, a, c);
  or or_1 (outt, and_1_out, and_2_out, and_3_out);
  and and_3 (and_3_out, a, b);
  and and_4 (and_4_out, not_1_out, c);
  and and_5 (and_5_out, a, not_2_out);
  or or_2 (err, and_4_out, and_5_out, and_6_out);
  and and_6 (and_6_out, b, not_3_out);
endmodule
