// Logisim project test_not_dff_tmr.circ as structural Verilog: 1 circuit, main circuit main
module main (
  input  in_1,
  input  a,
  input  b,
  input  c,
  output outt,
  output err
);

  wire and0_out, and1_out, and2_out, and3_out, and4_out, and5_out, not0_out, not1_out, not2_out, or0_out,
       or1_out;

  not not0 (not0_out, a);
  not not1 (not1_out, b);
  not not2 (not2_out, c);
  and and0 (and0_out, b, c);
  and and1 (and1_out, a, c);
  and and2 (and2_out, not0_out, c);
  and and3 (and3_out, a, not1_out);
  or or0 (or0_out, and0_out, and1_out);
  and and4 (and4_out, a, b);
  or or1 (or1_out, and2_out, and3_out);
  and and5 (and5_out, b, not2_out);
  or or2 (outt, or0_out, and4_out);
  or or3 (err, or1_out, and5_out);
endmodule
